# Fritzing sketch coffeebot (saved by Fritzing 0.9.3b)
breadboards: 1

parts:
  IC1 = Microchip MCP23008 8-bit I/O expander [part_number=MCP23008 package="DIP (Dual Inline) [THT]"]
  Raspberry_Pi_Zero1 = Raspberry Pi Zero
  R1 = Resistor [tolerance=±5% resistance=10k package=THT]
  C1 = Electrolytic Capacitor [capacitance=10µF package="100 mil [THT, electrolytic]"]  # not connected
  R2 = Resistor [tolerance=±5% resistance=10k package=THT]

nets:
  N1: IC1.SCL, Raspberry_Pi_Zero1.GPIO3
  N2: IC1.SDA, Raspberry_Pi_Zero1.GPIO2
  VSS: IC1.A2, IC1.A1, IC1.A0, IC1.VSS, Raspberry_Pi_Zero1.GND, R1.Pin_1, R2.Pin_1
  VDD: IC1.Reset, IC1.VDD, Raspberry_Pi_Zero1.5V

notes:
  CT Sensor

custom parts:
  Microchip MCP23008 8-bit I/O expander: Provides 8-bit, general purpose, parallel I/O expansion for I2C bus. Datasheet: http://ww1.microchip.com/downloads/en/devicedoc/21919e.pdf
